// Logisim project Alarma.circ as structural Verilog: 1 circuit, main circuit main
module main (
  input  activacion__x3,
  input  modo__x2,
  input  perimetral__x1,
  input  interior__x0,
  output sirena,
  output movimiento
);

  wire and_1_out, and_2_out, and_4_out;

  and and_1 (and_1_out, activacion__x3, perimetral__x1);
  and and_2 (and_2_out, activacion__x3, modo__x2);
  and and_3 (movimiento, activacion__x3, interior__x0);
  and and_4 (and_4_out, and_2_out, interior__x0);
  or or_1 (sirena, and_1_out, and_4_out);
endmodule
