// Logisim project Memoria.circ as structural Verilog: 7 circuits, main circuit main
module main (
  input  in_1,
  input  [7:0] offset,
  output [15:0] instruccion
);

  wire [7:0] contador_address;

  contador_seteable contador (.enciende_apaga(in_1), .offset(offset), .address(contador_address));
  ROM #(.dataWidth(16)) rom_1 (.addr(contador_address), .data(instruccion));  // open: sel

  // Notes on the sheet:
  //   contents of rom_1 (hex, n*v repeats v):
  //   0 1 2 3 4 5 6 7 8 9 10 11 12 13 14 15 16
endmodule

module contador_simple (
  output [7:0] out_1
);

  wire and_1_out, and_2_out, and_3_out, and_4_out, and_6_out, clock, ff;

  Clock clock_1 (.out(clock));
  T_Flip_Flop t_ff_1 (.clk(clock), .T(1'b1), .Q(out_1[0]));  // open: Qn, preset, reset, en
  T_Flip_Flop t_ff_2 (.clk(clock), .T(out_1[0]), .Q(out_1[1]));  // open: Qn, preset, reset, en
  T_Flip_Flop t_ff_3 (.clk(clock), .T(ff), .Q(out_1[4]));  // open: Qn, preset, reset, en
  and and_1 (and_1_out, out_1[1], out_1[0]);
  and and_2 (and_2_out, out_1[4], ff);
  T_Flip_Flop t_ff_4 (.clk(clock), .T(and_1_out), .Q(out_1[2]));  // open: Qn, preset, reset, en
  T_Flip_Flop t_ff_5 (.clk(clock), .T(and_2_out), .Q(out_1[5]));  // open: Qn, preset, reset, en
  and and_3 (and_3_out, out_1[2], and_1_out);
  and and_4 (and_4_out, out_1[5], and_2_out);
  T_Flip_Flop t_ff_6 (.clk(clock), .T(and_3_out), .Q(out_1[3]));  // open: Qn, preset, reset, en
  T_Flip_Flop t_ff_7 (.clk(clock), .T(and_4_out), .Q(out_1[6]));  // open: Qn, preset, reset, en
  and and_5 (ff, out_1[3], and_3_out);
  and and_6 (and_6_out, out_1[6], and_4_out);
  T_Flip_Flop t_ff_8 (.clk(clock), .T(and_6_out), .Q(out_1[7]));  // open: Qn, preset, reset, en
endmodule

module contador_seteable (
  input  enciende_apaga,
  input  [7:0] offset,
  output [7:0] address
);

  wire and_1_out, and_2_out, and_3_out, and_4_out, and_5_out, and_6_out, clock_1_out,
       set_address_contador_1_al_lsb, set_address_contador_1_out_4, set_address_contador_1_out_5,
       set_address_contador_1_out_6, set_address_contador_1_out_7, set_address_contador_1_out_8,
       set_address_contador_1_out_9, set_address_contador_1_out_10, set_address_contador_1_out_11,
       set_address_contador_1_out_12, set_address_contador_1_out_13, set_address_contador_1_out_14,
       set_address_contador_1_out_15, set_address_contador_1_out_16, set_address_contador_1_out_17,
       set_address_contador_1_out_18;

  Clock clock_1 (.out(clock_1_out));
  set_address_contador set_address_contador_1 (
    .enciende_apaga(enciende_apaga), .address(offset), .al_LSB(set_address_contador_1_al_lsb),
    .out_4(set_address_contador_1_out_4), .out_5(set_address_contador_1_out_5),
    .out_6(set_address_contador_1_out_6), .out_7(set_address_contador_1_out_7),
    .out_8(set_address_contador_1_out_8), .out_9(set_address_contador_1_out_9),
    .out_10(set_address_contador_1_out_10), .out_11(set_address_contador_1_out_11),
    .out_12(set_address_contador_1_out_12), .out_13(set_address_contador_1_out_13),
    .out_14(set_address_contador_1_out_14), .out_15(set_address_contador_1_out_15),
    .out_16(set_address_contador_1_out_16), .out_17(set_address_contador_1_out_17),
    .out_18(set_address_contador_1_out_18));
  T_Flip_Flop t_ff_1 (
    .clk(clock_1_out), .T(1'b1), .Q(address[0]), .preset(set_address_contador_1_al_lsb),
    .reset(set_address_contador_1_out_4));  // open: Qn, en
  T_Flip_Flop t_ff_2 (
    .clk(clock_1_out), .T(address[0]), .Q(address[1]), .preset(set_address_contador_1_out_5),
    .reset(set_address_contador_1_out_6));  // open: Qn, en
  and and_1 (and_1_out, address[1], address[0]);
  T_Flip_Flop t_ff_3 (
    .clk(clock_1_out), .T(and_1_out), .Q(address[2]), .preset(set_address_contador_1_out_7),
    .reset(set_address_contador_1_out_8));  // open: Qn, en
  and and_2 (and_2_out, address[2], and_1_out);
  T_Flip_Flop t_ff_4 (
    .clk(clock_1_out), .T(and_2_out), .Q(address[3]), .preset(set_address_contador_1_out_9),
    .reset(set_address_contador_1_out_10));  // open: Qn, en
  and and_3 (and_3_out, address[3], and_2_out);
  T_Flip_Flop t_ff_5 (
    .clk(clock_1_out), .T(and_3_out), .Q(address[4]), .preset(set_address_contador_1_out_11),
    .reset(set_address_contador_1_out_12));  // open: Qn, en
  and and_4 (and_4_out, address[4], and_3_out);
  T_Flip_Flop t_ff_6 (
    .clk(clock_1_out), .T(and_4_out), .Q(address[5]), .preset(set_address_contador_1_out_13),
    .reset(set_address_contador_1_out_14));  // open: Qn, en
  and and_5 (and_5_out, address[5], and_4_out);
  T_Flip_Flop t_ff_7 (
    .clk(clock_1_out), .T(and_5_out), .Q(address[6]), .preset(set_address_contador_1_out_15),
    .reset(set_address_contador_1_out_16));  // open: Qn, en
  and and_6 (and_6_out, address[6], and_5_out);
  T_Flip_Flop t_ff_8 (
    .clk(clock_1_out), .T(and_6_out), .Q(address[7]), .preset(set_address_contador_1_out_17),
    .reset(set_address_contador_1_out_18));  // open: Qn, en
endmodule

module set_address_contador (
  input  enciende_apaga,
  input  [7:0] address,
  output al_LSB,
  output out_4,
  output out_5,
  output out_6,
  output out_7,
  output out_8,
  output out_9,
  output out_10,
  output out_11,
  output out_12,
  output out_13,
  output out_14,
  output out_15,
  output out_16,
  output out_17,
  output out_18
);

  Demultiplexer demultiplexer_1 (.out0(out_4), .out1(al_LSB), .in(1'b1), .sel(address[0]), .en(enciende_apaga));
  Demultiplexer demultiplexer_2 (.out0(out_6), .out1(out_5), .in(1'b1), .sel(address[1]), .en(enciende_apaga));
  Demultiplexer demultiplexer_3 (.out0(out_8), .out1(out_7), .in(1'b1), .sel(address[2]), .en(enciende_apaga));
  Demultiplexer demultiplexer_4 (.out0(out_10), .out1(out_9), .in(1'b1), .sel(address[3]), .en(enciende_apaga));
  Demultiplexer demultiplexer_5 (.out0(out_12), .out1(out_11), .in(1'b1), .sel(address[4]), .en(enciende_apaga));
  Demultiplexer demultiplexer_6 (.out0(out_14), .out1(out_13), .in(1'b1), .sel(address[5]), .en(enciende_apaga));
  Demultiplexer demultiplexer_7 (.out0(out_16), .out1(out_15), .in(1'b1), .sel(address[6]), .en(enciende_apaga));
  Demultiplexer demultiplexer_8 (.out0(out_18), .out1(out_17), .in(1'b1), .sel(address[7]), .en(enciende_apaga));
endmodule

module latch_S_R (
  input  Preset,
  input  e1,
  input  Habilitacion,
  input  e2,
  input  Reset,
  output Q,
  output minus_Q
);

  wire nand_1_out, nand_2_out, nand_3_out, nand_4_out;

  nand nand_1 (nand_1_out, e1, Habilitacion);
  nand nand_2 (nand_2_out, Habilitacion, e2);
  nand nand_3 (nand_3_out, nand_1_out, minus_Q);
  nand nand_4 (nand_4_out, Q, nand_2_out);
  or or_1 (Q, Preset, nand_3_out);
  or or_2 (minus_Q, nand_4_out, Reset);
endmodule

module latch_D (
  input  preset,
  input  D,
  input  H,
  input  reset,
  output Q,
  output minus_Q
);

  wire not_1_out;

  not not_1 (not_1_out, D);
  latch_S_R latch_s_r_1 (
    .e1(D), .Habilitacion(H), .e2(not_1_out), .Preset(preset), .Reset(reset), .Q(Q), .minus_Q(minus_Q));
endmodule

module FF_D_con_latch_D (
  input  D,
  output Q,
  output minus_Q
);

  wire clock_1_out, latch_d_1_q, not_1_out;

  latch_D latch_d_1 (.D(D), .H(not_1_out), .Q(latch_d_1_q));  // open: preset, reset, minus_Q
  not not_1 (not_1_out, clock_1_out);
  latch_D latch_d_2 (.D(latch_d_1_q), .H(clock_1_out), .Q(Q), .minus_Q(minus_Q));  // open: preset, reset
  Clock clock_1 (.out(clock_1_out));
endmodule
