// Logisim project procesador.circ as structural Verilog: 8 circuits, main circuit main
module main (
  input  [7:0] j_address,
  input  j_enable,
  input  in_3,
  input  [7:0] \input ,
  input  [7:0] salida,
  output [15:0] salida_2,
  output [7:0] out_7,
  output carry_out
);

  wire alu_op0, alu_op1, alu_op2, clock, imm_we, in_en, out_we, reg_en, reg_we, regA_we;
  wire [7:0] alu_1_salida, bancoreg_1_salida, ir_1__0_7, ir_1__8_15, registro_2_salida;

  Clock Reloj (.out(clock));
  DU du_1 (
    .IR13(ir_1__8_15[5]), .IR12(ir_1__8_15[4]), .IR11(ir_1__8_15[3]), .IR10(ir_1__8_15[2]),
    .IR09(ir_1__8_15[1]), .IR08(ir_1__8_15[0]), .reg_en(reg_en), .alu_op2(alu_op2), .alu_op1(alu_op1),
    .regA_we(regA_we), .out_we(out_we), .reg_we(reg_we), .in_en(in_en), .alu_op0(alu_op0), .inm_we(imm_we));
  Registro registro_1 (.clock(clock), .reset(in_3), .we(out_we), .salida(salida));  // open: entrada
  IR ir_1 (.entrada(salida_2), .reset(in_3), .we(1'b1), .clock(clock), ._0_7(ir_1__0_7), ._8_15(ir_1__8_15));
  BancoReg bancoreg_1 (
    .rs(ir_1__0_7[3:0]), .rd(ir_1__0_7[7:4]), .we(reg_we), .salida(bancoreg_1_salida), .reset(in_3),
    .clock(clock), .entrada(alu_1_salida));
  ROM rom_1 (.clock(clock), .j_enable(j_enable), .j_address(j_address), .instruccion(salida_2));
  assign out_7 = imm_we ? ir_1__0_7 : 8'bz;  // Controlled_Buffer controlled_buffer_1
  assign out_7 = reg_en ? bancoreg_1_salida : 8'bz;  // Controlled_Buffer controlled_buffer_2
  assign out_7 = in_en ? \input  : 8'bz;  // Controlled_Buffer controlled_buffer_3
  Registro registro_2 (.entrada(out_7), .clock(clock), .reset(in_3), .we(regA_we), .salida(registro_2_salida));
  ALU alu_1 (
    .a(out_7), .b(registro_2_salida), .carry_out(carry_out), .sel1(alu_op0), .sel2(alu_op1), .sel3(alu_op2),
    .salida(alu_1_salida));

  // Other names for the same wires on the sheet: reset = in_3
endmodule

module DU (
  input  IR13,
  input  IR12,
  input  IR11,
  input  IR10,
  input  IR09,
  input  IR08,
  output reg_en,
  output alu_op2,
  output alu_op1,
  output regA_we,
  output out_we,
  output reg_we,
  output in_en,
  output alu_op0,
  output inm_we
);

  wire and_1_out, and_2_out, and_3_out, and_4_out, and_5_out, and_6_out, and_7_out, and_8_out, and_9_out,
       and_10_out, and_11_out, and_12_out, and_13_out, and_14_out, and_15_out, and_16_out, and_17_out,
       and_18_out, and_19_out, and_20_out, and_21_out, and_22_out, and_23_out, and_24_out, and_25_out,
       and_26_out, and_27_out, and_28_out, and_29_out, and_30_out, and_31_out, and_32_out, and_33_out,
       and_34_out, and_35_out, and_36_out, and_37_out, and_38_out, and_39_out, and_40_out, and_41_out,
       and_42_out, and_43_out, and_44_out, and_45_out, and_46_out, and_47_out, and_48_out, and_49_out,
       and_50_out, and_51_out, and_52_out, and_53_out, and_54_out, and_55_out, and_56_out, and_57_out,
       and_58_out, and_59_out, and_60_out, and_61_out, and_62_out, and_63_out, and_64_out, and_65_out,
       and_66_out, and_67_out, and_68_out, and_69_out, and_70_out, and_71_out, and_72_out, and_73_out,
       and_74_out, and_76_out, and_77_out, and_78_out, and_79_out, and_81_out, and_82_out, and_83_out,
       and_84_out, and_86_out, and_87_out, and_88_out, not_1_out, not_2_out, not_3_out, not_4_out, not_5_out,
       not_6_out, not_7_out, not_8_out, not_9_out, not_10_out, not_11_out, not_12_out, not_13_out,
       not_14_out, not_15_out, not_16_out, not_17_out, not_18_out, not_19_out, not_20_out, not_21_out,
       not_22_out, not_23_out, not_24_out, not_25_out, not_26_out, not_27_out, not_28_out, not_29_out,
       not_30_out, not_31_out, not_32_out, not_33_out, not_34_out, not_35_out, not_36_out, not_37_out,
       not_38_out, not_39_out, not_40_out, not_41_out, not_42_out, not_43_out, not_44_out, not_45_out,
       not_46_out, not_47_out, not_48_out, not_49_out, not_50_out, not_51_out, not_52_out, not_53_out,
       not_54_out, not_55_out, not_56_out, not_57_out, not_58_out, not_59_out, not_60_out, not_61_out,
       not_62_out, not_63_out, not_64_out, not_65_out, not_66_out, not_67_out, not_68_out, not_69_out,
       not_70_out, not_71_out, not_72_out, not_73_out, not_74_out, not_75_out, not_76_out, not_77_out,
       not_78_out, not_79_out, not_80_out, or_1_out, or_3_out, or_5_out, or_8_out, or_10_out, or_11_out;

  not not_1 (not_1_out, IR13);
  not not_2 (not_2_out, IR12);
  not not_3 (not_3_out, IR11);
  not not_4 (not_4_out, IR13);
  not not_5 (not_5_out, IR12);
  not not_6 (not_6_out, IR11);
  not not_7 (not_7_out, IR13);
  not not_8 (not_8_out, IR12);
  not not_9 (not_9_out, IR13);
  not not_10 (not_10_out, IR12);
  not not_11 (not_11_out, IR13);
  not not_12 (not_12_out, IR12);
  not not_13 (not_13_out, IR09);
  not not_14 (not_14_out, IR13);
  not not_15 (not_15_out, IR12);
  not not_16 (not_16_out, IR13);
  not not_17 (not_17_out, IR12);
  not not_18 (not_18_out, IR10);
  not not_19 (not_19_out, IR13);
  not not_20 (not_20_out, IR12);
  not not_21 (not_21_out, IR09);
  not not_22 (not_22_out, IR13);
  not not_23 (not_23_out, IR12);
  not not_24 (not_24_out, IR10);
  not not_25 (not_25_out, IR09);
  not not_26 (not_26_out, IR13);
  not not_27 (not_27_out, IR12);
  not not_28 (not_28_out, IR13);
  not not_29 (not_29_out, IR12);
  not not_30 (not_30_out, IR13);
  not not_31 (not_31_out, IR12);
  not not_32 (not_32_out, IR10);
  not not_33 (not_33_out, IR09);
  not not_34 (not_34_out, IR13);
  not not_35 (not_35_out, IR12);
  not not_36 (not_36_out, IR13);
  not not_37 (not_37_out, IR12);
  not not_38 (not_38_out, IR13);
  not not_39 (not_39_out, IR12);
  not not_40 (not_40_out, IR09);
  and and_1 (and_1_out, not_1_out, not_2_out);
  and and_2 (and_2_out, not_3_out, IR08);
  and and_3 (and_3_out, not_4_out, not_5_out);
  and and_4 (and_4_out, not_6_out, IR09);
  not not_41 (not_41_out, IR13);
  not not_42 (not_42_out, IR12);
  not not_43 (not_43_out, IR10);
  and and_5 (and_5_out, not_7_out, not_8_out);
  not not_44 (not_44_out, IR11);
  and and_6 (and_6_out, IR10, IR09);
  and and_7 (and_7_out, not_9_out, not_10_out);
  not not_45 (not_45_out, IR10);
  not not_46 (not_46_out, IR09);
  not not_47 (not_47_out, IR13);
  not not_48 (not_48_out, IR12);
  and and_8 (and_8_out, not_11_out, not_12_out);
  not not_49 (not_49_out, IR11);
  and and_9 (and_9_out, IR10, not_13_out);
  and and_10 (and_10_out, not_14_out, not_15_out);
  not not_50 (not_50_out, IR11);
  and and_11 (and_11_out, IR10, IR09);
  not not_51 (not_51_out, IR08);
  not not_52 (not_52_out, IR13);
  not not_53 (not_53_out, IR12);
  and and_12 (and_12_out, not_16_out, not_17_out);
  not not_54 (not_54_out, IR11);
  and and_13 (and_13_out, not_18_out, IR09);
  and and_14 (and_14_out, not_19_out, not_20_out);
  not not_55 (not_55_out, IR11);
  and and_15 (and_15_out, IR10, not_21_out);
  not not_56 (not_56_out, IR08);
  and and_16 (and_16_out, not_22_out, not_23_out);
  not not_57 (not_57_out, IR11);
  and and_17 (and_17_out, not_24_out, not_25_out);
  not not_58 (not_58_out, IR13);
  not not_59 (not_59_out, IR12);
  not not_60 (not_60_out, IR10);
  not not_61 (not_61_out, IR08);
  and and_18 (and_18_out, not_26_out, not_27_out);
  not not_62 (not_62_out, IR11);
  not not_63 (not_63_out, IR08);
  and and_19 (and_19_out, not_28_out, not_29_out);
  not not_64 (not_64_out, IR11);
  not not_65 (not_65_out, IR13);
  not not_66 (not_66_out, IR12);
  not not_67 (not_67_out, IR10);
  and and_20 (and_20_out, not_30_out, not_31_out);
  not not_68 (not_68_out, IR11);
  and and_21 (and_21_out, not_32_out, not_33_out);
  not not_69 (not_69_out, IR08);
  and and_22 (and_22_out, not_34_out, not_35_out);
  not not_70 (not_70_out, IR11);
  and and_23 (and_23_out, IR10, IR09);
  not not_71 (not_71_out, IR08);
  and and_24 (and_24_out, not_36_out, not_37_out);
  not not_72 (not_72_out, IR10);
  not not_73 (not_73_out, IR08);
  not not_74 (not_74_out, IR13);
  not not_75 (not_75_out, IR12);
  and and_25 (and_25_out, not_38_out, not_39_out);
  not not_76 (not_76_out, IR11);
  and and_26 (and_26_out, IR10, not_40_out);
  not not_77 (not_77_out, IR08);
  and and_27 (and_27_out, and_1_out, and_2_out);
  and and_28 (and_28_out, and_3_out, and_4_out);
  and and_29 (and_29_out, not_41_out, not_42_out);
  and and_30 (and_30_out, IR11, not_43_out);
  and and_31 (and_31_out, and_5_out, not_44_out);
  and and_32 (and_32_out, and_6_out, IR08);
  and and_33 (and_33_out, and_7_out, IR11);
  and and_34 (and_34_out, not_45_out, not_46_out);
  and and_35 (and_35_out, not_47_out, not_48_out);
  not not_78 (not_78_out, IR10);
  and and_36 (and_36_out, and_8_out, not_49_out);
  and and_37 (and_37_out, and_9_out, IR08);
  and and_38 (and_38_out, and_10_out, not_50_out);
  and and_39 (and_39_out, and_11_out, not_51_out);
  and and_40 (and_40_out, not_52_out, not_53_out);
  not not_79 (not_79_out, IR10);
  and and_41 (and_41_out, and_12_out, not_54_out);
  and and_42 (and_42_out, and_13_out, IR08);
  and and_43 (and_43_out, and_14_out, not_55_out);
  and and_44 (and_44_out, and_15_out, not_56_out);
  and and_45 (and_45_out, and_16_out, not_57_out);
  and and_46 (and_46_out, and_17_out, IR08);
  and and_47 (and_47_out, not_58_out, not_59_out);
  and and_48 (and_48_out, not_60_out, not_61_out);
  and and_49 (and_49_out, and_18_out, not_62_out);
  and and_50 (and_50_out, IR09, not_63_out);
  and and_51 (and_51_out, and_19_out, not_64_out);
  and and_52 (and_52_out, IR10, IR08);
  and and_53 (and_53_out, not_65_out, not_66_out);
  and and_54 (and_54_out, IR11, not_67_out);
  and and_55 (and_55_out, and_20_out, not_68_out);
  and and_56 (and_56_out, and_21_out, not_69_out);
  and and_57 (and_57_out, and_22_out, not_70_out);
  and and_58 (and_58_out, and_23_out, not_71_out);
  and and_59 (and_59_out, and_24_out, IR11);
  and and_60 (and_60_out, not_72_out, not_73_out);
  and and_61 (and_61_out, not_74_out, not_75_out);
  not not_80 (not_80_out, IR10);
  and and_62 (and_62_out, and_25_out, not_76_out);
  and and_63 (and_63_out, and_26_out, not_77_out);
  or or_1 (or_1_out, and_27_out, and_28_out);
  and and_64 (and_64_out, and_29_out, and_30_out);
  and and_65 (and_65_out, and_31_out, and_32_out);
  and and_66 (and_66_out, and_33_out, and_34_out);
  and and_67 (and_67_out, and_35_out, IR11);
  and and_68 (and_68_out, not_78_out, IR08);
  and and_69 (and_69_out, and_36_out, and_37_out);
  and and_70 (and_70_out, and_38_out, and_39_out);
  and and_71 (and_71_out, and_40_out, IR11);
  and and_72 (and_72_out, not_79_out, IR08);
  and and_73 (and_73_out, and_41_out, and_42_out);
  and and_74 (and_74_out, and_43_out, and_44_out);
  and and_75 (out_we, and_45_out, and_46_out);
  and and_76 (and_76_out, and_47_out, and_48_out);
  and and_77 (and_77_out, and_49_out, and_50_out);
  and and_78 (and_78_out, and_51_out, and_52_out);
  and and_79 (and_79_out, and_53_out, and_54_out);
  and and_80 (in_en, and_55_out, and_56_out);
  and and_81 (and_81_out, and_57_out, and_58_out);
  and and_82 (and_82_out, and_59_out, and_60_out);
  and and_83 (and_83_out, and_61_out, IR11);
  and and_84 (and_84_out, not_80_out, IR09);
  and and_85 (inm_we, and_62_out, and_63_out);
  or or_2 (reg_en, or_1_out, and_64_out);
  or or_3 (or_3_out, and_65_out, and_66_out);
  or or_4 (alu_op2, or_3_out, and_86_out);
  and and_86 (and_86_out, and_67_out, and_68_out);
  or or_5 (or_5_out, and_69_out, and_70_out);
  or or_6 (alu_op1, or_5_out, and_87_out);
  and and_87 (and_87_out, and_71_out, and_72_out);
  or or_7 (regA_we, and_73_out, and_74_out);
  or or_8 (or_8_out, and_76_out, and_77_out);
  or or_9 (reg_we, or_8_out, or_10_out);
  or or_10 (or_10_out, and_78_out, and_79_out);
  or or_11 (or_11_out, and_81_out, and_82_out);
  or or_12 (alu_op0, or_11_out, and_88_out);
  and and_88 (and_88_out, and_83_out, and_84_out);
endmodule

// Reg_out
module Registro (
  input  clock,
  input  reset,
  input  [7:0] entrada,
  input  we,
  output [7:0] salida
);

  wire [7:0] controlled_buffer_1_out;

  assign controlled_buffer_1_out = we ? entrada : 8'bz;  // Controlled_Buffer controlled_buffer_1
  D_Flip_Flop d_ff_1 (
    .clk(clock), .D(controlled_buffer_1_out[0]), .Q(salida[0]), .reset(reset));  // open: Qn, preset, en
  D_Flip_Flop d_ff_2 (
    .clk(clock), .D(controlled_buffer_1_out[1]), .Q(salida[1]), .reset(reset));  // open: Qn, preset, en
  D_Flip_Flop d_ff_3 (
    .clk(clock), .D(controlled_buffer_1_out[2]), .Q(salida[2]), .reset(reset));  // open: Qn, preset, en
  D_Flip_Flop d_ff_4 (
    .clk(clock), .D(controlled_buffer_1_out[3]), .Q(salida[3]), .reset(reset));  // open: Qn, preset, en
  D_Flip_Flop d_ff_5 (
    .clk(clock), .D(controlled_buffer_1_out[4]), .Q(salida[4]), .reset(reset));  // open: Qn, preset, en
  D_Flip_Flop d_ff_6 (
    .clk(clock), .D(controlled_buffer_1_out[5]), .Q(salida[5]), .reset(reset));  // open: Qn, preset, en
  D_Flip_Flop d_ff_7 (
    .clk(clock), .D(controlled_buffer_1_out[6]), .Q(salida[6]), .reset(reset));  // open: Qn, preset, en
  D_Flip_Flop d_ff_8 (
    .clk(clock), .D(controlled_buffer_1_out[7]), .Q(salida[7]), .reset(reset));  // open: Qn, preset, en
endmodule

module IR (
  input  reset,
  input  [15:0] entrada,
  input  we,
  input  clock,
  output [7:0] _0_7,
  output [7:0] _8_15
);

  wire [7:0] controlled_buffer_1_out, controlled_buffer_2_out;

  assign controlled_buffer_1_out = we ? entrada[7:0] : 8'bz;  // Controlled_Buffer controlled_buffer_1
  assign controlled_buffer_2_out = we ? entrada[15:8] : 8'bz;  // Controlled_Buffer controlled_buffer_2
  Registro registro_1 (.entrada(controlled_buffer_1_out), .clock(clock), .reset(reset), .salida(_0_7));  // open: we
  Registro registro_2 (.entrada(controlled_buffer_2_out), .clock(clock), .reset(reset), .salida(_8_15));  // open: we
endmodule

module ALU (
  input  [7:0] a,
  input  [7:0] b,
  input  sel1,
  input  sel2,
  input  sel3,
  output carry_out,
  output [7:0] salida
);

  wire [7:0] and_x8_1_out_3, desplazar_derecha_1_out_2, desplazar_izq_1_out_2, full_adder_8bits_1_r,
       or_x8_1_out_3, xor_x8_1_out_3, xor_x8_2_out_3;

  desplazar_izq desplazar_izq_1 (.in_1(a), .out_2(desplazar_izq_1_out_2));
  XOR_x8 xor_x8_1 (.in_1(b), .in_2({8{sel3}}), .out_3(xor_x8_1_out_3));
  AND_x8 and_x8_1 (.in_1(a), .in_2(b), .out_3(and_x8_1_out_3));
  full_adder_8bits full_adder_8bits_1 (
    .in_1(sel3), .B(a), .A(xor_x8_1_out_3), .R(full_adder_8bits_1_r), .out_5(carry_out));
  OR_x8 or_x8_1 (.in_1(a), .in_2(b), .out_3(or_x8_1_out_3));
  XOR_x8 xor_x8_2 (.in_1(a), .in_2(b), .out_3(xor_x8_2_out_3));
  desplazar_derecha desplazar_derecha_1 (.in_1(a), .out_2(desplazar_derecha_1_out_2));
  mux_4x8_8 mux_4x8_8_1 (
    .in_1(a), .in_2(desplazar_izq_1_out_2), .in_3(full_adder_8bits_1_r), .in_4(full_adder_8bits_1_r),
    .in_5(and_x8_1_out_3), .in_6(or_x8_1_out_3), .in_7(xor_x8_2_out_3), .in_8(desplazar_derecha_1_out_2),
    .in_9(sel1), .in_10(sel2), .in_11(sel3), .out_12(salida));

  // Other names for the same wires on the sheet: t1 = sel3; t2[7:0] = {8{sel3}}

  // Notes on the sheet:
  //   0
  //   0
  //   0
  //   0
  //   0
  //   1
  //   1
  //   0
  //   1
  //   0
  //   0
  //   1
  //   1
  //   1
  //   1
  //   1
  //   0
  //   1
  //   0
  //   1
  //   0
  //   1
  //   0
  //   1
  //   a
  //   a << 1
  //   a + b
  //   a - b
  //   a and b
  //   a or b
  //   a xor b
  //   a >> 1
endmodule

module BancoReg (
  input  [3:0] rs,
  input  reset,
  input  clock,
  input  [7:0] entrada,
  input  [3:0] rd,
  input  we,
  output [7:0] salida
);

  wire demultiplexer_1_out0, demultiplexer_1_out1, demultiplexer_1_out2, demultiplexer_1_out3,
       demultiplexer_1_out4, demultiplexer_1_out5, demultiplexer_1_out6, demultiplexer_1_out7,
       demultiplexer_1_out8, demultiplexer_1_out9, demultiplexer_1_out10, demultiplexer_1_out11,
       demultiplexer_1_out12, demultiplexer_1_out13, demultiplexer_1_out14, demultiplexer_1_out15,
       demultiplexer_2_out0, demultiplexer_2_out1, demultiplexer_2_out2, demultiplexer_2_out3,
       demultiplexer_2_out4, demultiplexer_2_out5, demultiplexer_2_out6, demultiplexer_2_out7,
       demultiplexer_2_out8, demultiplexer_2_out9, demultiplexer_2_out10, demultiplexer_2_out11,
       demultiplexer_2_out12, demultiplexer_2_out13, demultiplexer_2_out14, demultiplexer_2_out15;
  wire [7:0] registro_1_salida, registro_2_salida, registro_3_salida, registro_4_salida, registro_5_salida,
       registro_6_salida, registro_7_salida, registro_8_salida, registro_9_salida, registro_10_salida,
       registro_11_salida, registro_12_salida, registro_13_salida, registro_14_salida, registro_15_salida,
       registro_16_salida;

  assign salida = demultiplexer_1_out0 ? registro_1_salida : 8'bz;  // Controlled_Buffer controlled_buffer_1
  Registro registro_1 (
    .entrada(entrada), .clock(clock), .reset(reset), .we(demultiplexer_2_out0), .salida(registro_1_salida));
  assign salida = demultiplexer_1_out1 ? registro_2_salida : 8'bz;  // Controlled_Buffer controlled_buffer_2
  Registro registro_2 (
    .entrada(entrada), .clock(clock), .reset(reset), .we(demultiplexer_2_out1), .salida(registro_2_salida));
  assign salida = demultiplexer_1_out2 ? registro_3_salida : 8'bz;  // Controlled_Buffer controlled_buffer_3
  Registro registro_3 (
    .entrada(entrada), .clock(clock), .reset(reset), .we(demultiplexer_2_out2), .salida(registro_3_salida));
  assign salida = demultiplexer_1_out3 ? registro_4_salida : 8'bz;  // Controlled_Buffer controlled_buffer_4
  Registro registro_4 (
    .entrada(entrada), .clock(clock), .reset(reset), .we(demultiplexer_2_out3), .salida(registro_4_salida));
  assign salida = demultiplexer_1_out5 ? registro_6_salida : 8'bz;  // Controlled_Buffer controlled_buffer_5
  assign salida = demultiplexer_1_out4 ? registro_5_salida : 8'bz;  // Controlled_Buffer controlled_buffer_6
  Registro registro_5 (
    .entrada(entrada), .clock(clock), .reset(reset), .we(demultiplexer_2_out4), .salida(registro_5_salida));
  Registro registro_6 (
    .entrada(entrada), .clock(clock), .reset(reset), .we(demultiplexer_2_out5), .salida(registro_6_salida));
  assign salida = demultiplexer_1_out6 ? registro_7_salida : 8'bz;  // Controlled_Buffer controlled_buffer_7
  Registro registro_7 (
    .entrada(entrada), .clock(clock), .reset(reset), .we(demultiplexer_2_out6), .salida(registro_7_salida));
  Demultiplexer #(.select(4)) demultiplexer_1 (
    .out0(demultiplexer_1_out0), .out1(demultiplexer_1_out1), .out2(demultiplexer_1_out2),
    .out3(demultiplexer_1_out3), .out4(demultiplexer_1_out4), .out5(demultiplexer_1_out5),
    .out6(demultiplexer_1_out6), .out7(demultiplexer_1_out7), .out8(demultiplexer_1_out8),
    .out9(demultiplexer_1_out9), .out10(demultiplexer_1_out10), .out11(demultiplexer_1_out11),
    .out12(demultiplexer_1_out12), .out13(demultiplexer_1_out13), .out14(demultiplexer_1_out14),
    .out15(demultiplexer_1_out15), .in(1'b1), .sel(rs));  // open: en
  assign salida = demultiplexer_1_out7 ? registro_8_salida : 8'bz;  // Controlled_Buffer controlled_buffer_8
  Registro registro_8 (
    .entrada(entrada), .clock(clock), .reset(reset), .we(demultiplexer_2_out7), .salida(registro_8_salida));
  Demultiplexer #(.select(4)) demultiplexer_2 (
    .out0(demultiplexer_2_out0), .out1(demultiplexer_2_out1), .out2(demultiplexer_2_out2),
    .out3(demultiplexer_2_out3), .out4(demultiplexer_2_out4), .out5(demultiplexer_2_out5),
    .out6(demultiplexer_2_out6), .out7(demultiplexer_2_out7), .out8(demultiplexer_2_out8),
    .out9(demultiplexer_2_out9), .out10(demultiplexer_2_out10), .out11(demultiplexer_2_out11),
    .out12(demultiplexer_2_out12), .out13(demultiplexer_2_out13), .out14(demultiplexer_2_out14),
    .out15(demultiplexer_2_out15), .in(we), .sel(rd));  // open: en
  assign salida = demultiplexer_1_out8 ? registro_9_salida : 8'bz;  // Controlled_Buffer controlled_buffer_9
  Registro registro_9 (
    .entrada(entrada), .clock(clock), .reset(reset), .we(demultiplexer_2_out8), .salida(registro_9_salida));
  assign salida = demultiplexer_1_out9 ? registro_10_salida : 8'bz;  // Controlled_Buffer controlled_buffer_10
  Registro registro_10 (
    .entrada(entrada), .clock(clock), .reset(reset), .we(demultiplexer_2_out9), .salida(registro_10_salida));
  assign salida = demultiplexer_1_out10 ? registro_11_salida : 8'bz;  // Controlled_Buffer controlled_buffer_11
  Registro registro_11 (
    .entrada(entrada), .clock(clock), .reset(reset), .we(demultiplexer_2_out10), .salida(registro_11_salida));
  assign salida = demultiplexer_1_out11 ? registro_12_salida : 8'bz;  // Controlled_Buffer controlled_buffer_12
  Registro registro_12 (
    .entrada(entrada), .clock(clock), .reset(reset), .we(demultiplexer_2_out11), .salida(registro_12_salida));
  assign salida = demultiplexer_1_out13 ? registro_14_salida : 8'bz;  // Controlled_Buffer controlled_buffer_13
  assign salida = demultiplexer_1_out12 ? registro_13_salida : 8'bz;  // Controlled_Buffer controlled_buffer_14
  Registro registro_13 (
    .entrada(entrada), .clock(clock), .reset(reset), .we(demultiplexer_2_out12), .salida(registro_13_salida));
  Registro registro_14 (
    .entrada(entrada), .clock(clock), .reset(reset), .we(demultiplexer_2_out13), .salida(registro_14_salida));
  assign salida = demultiplexer_1_out14 ? registro_15_salida : 8'bz;  // Controlled_Buffer controlled_buffer_15
  Registro registro_15 (
    .entrada(entrada), .clock(clock), .reset(reset), .we(demultiplexer_2_out14), .salida(registro_15_salida));
  assign salida = demultiplexer_1_out15 ? registro_16_salida : 8'bz;  // Controlled_Buffer controlled_buffer_16
  Registro registro_16 (
    .entrada(entrada), .clock(clock), .reset(reset), .we(demultiplexer_2_out15), .salida(registro_16_salida));
endmodule

module ROM (
  input  clock,
  input  j_enable,
  input  [7:0] j_address,
  output [15:0] instruccion
);

  wire [7:0] contador_1_address;

  contador contador_1 (.clock(clock), .jump_enable(j_enable), .j_address(j_address), .address(contador_1_address));
  ROM_part #(.dataWidth(16)) rom_1 (.addr(contador_1_address), .data(instruccion));  // open: sel

  // Notes on the sheet:
  //   contents of rom_1 (hex, n*v repeats v):
  //   130 140 50a 1054 1364 2176 207 206 205
endmodule

module contador (
  input  clock,
  input  jump_enable,
  input  [7:0] j_address,
  output [7:0] address
);

  wire and_1_out, and_2_out, and_3_out, and_4_out, and_5_out, and_6_out, set_address_contador_1_al_lsb,
       set_address_contador_1_out_4, set_address_contador_1_out_5, set_address_contador_1_out_6,
       set_address_contador_1_out_7, set_address_contador_1_out_8, set_address_contador_1_out_9,
       set_address_contador_1_out_10, set_address_contador_1_out_11, set_address_contador_1_out_12,
       set_address_contador_1_out_13, set_address_contador_1_out_14, set_address_contador_1_out_15,
       set_address_contador_1_out_16, set_address_contador_1_out_17, set_address_contador_1_out_18;

  set_address_contador set_address_contador_1 (
    .enciende_apaga(jump_enable), .address(j_address), .al_LSB(set_address_contador_1_al_lsb),
    .out_4(set_address_contador_1_out_4), .out_5(set_address_contador_1_out_5),
    .out_6(set_address_contador_1_out_6), .out_7(set_address_contador_1_out_7),
    .out_8(set_address_contador_1_out_8), .out_9(set_address_contador_1_out_9),
    .out_10(set_address_contador_1_out_10), .out_11(set_address_contador_1_out_11),
    .out_12(set_address_contador_1_out_12), .out_13(set_address_contador_1_out_13),
    .out_14(set_address_contador_1_out_14), .out_15(set_address_contador_1_out_15),
    .out_16(set_address_contador_1_out_16), .out_17(set_address_contador_1_out_17),
    .out_18(set_address_contador_1_out_18));
  T_Flip_Flop t_ff_1 (
    .clk(clock), .T(1'b1), .Q(address[0]), .preset(set_address_contador_1_al_lsb),
    .reset(set_address_contador_1_out_4));  // open: Qn, en
  T_Flip_Flop t_ff_2 (
    .clk(clock), .T(address[0]), .Q(address[1]), .preset(set_address_contador_1_out_5),
    .reset(set_address_contador_1_out_6));  // open: Qn, en
  and and_1 (and_1_out, address[1], address[0]);
  T_Flip_Flop t_ff_3 (
    .clk(clock), .T(and_1_out), .Q(address[2]), .preset(set_address_contador_1_out_7),
    .reset(set_address_contador_1_out_8));  // open: Qn, en
  and and_2 (and_2_out, address[2], and_1_out);
  T_Flip_Flop t_ff_4 (
    .clk(clock), .T(and_2_out), .Q(address[3]), .preset(set_address_contador_1_out_9),
    .reset(set_address_contador_1_out_10));  // open: Qn, en
  and and_3 (and_3_out, address[3], and_2_out);
  T_Flip_Flop t_ff_5 (
    .clk(clock), .T(and_3_out), .Q(address[4]), .preset(set_address_contador_1_out_11),
    .reset(set_address_contador_1_out_12));  // open: Qn, en
  and and_4 (and_4_out, address[4], and_3_out);
  T_Flip_Flop t_ff_6 (
    .clk(clock), .T(and_4_out), .Q(address[5]), .preset(set_address_contador_1_out_13),
    .reset(set_address_contador_1_out_14));  // open: Qn, en
  and and_5 (and_5_out, address[5], and_4_out);
  T_Flip_Flop t_ff_7 (
    .clk(clock), .T(and_5_out), .Q(address[6]), .preset(set_address_contador_1_out_15),
    .reset(set_address_contador_1_out_16));  // open: Qn, en
  and and_6 (and_6_out, address[6], and_5_out);
  T_Flip_Flop t_ff_8 (
    .clk(clock), .T(and_6_out), .Q(address[7]), .preset(set_address_contador_1_out_17),
    .reset(set_address_contador_1_out_18));  // open: Qn, en
endmodule
