// Logisim project procesador_ok.circ as structural Verilog: 14 circuits, main circuit main
module main (
  input  in_1,
  input  [7:0] in_2,
  output [7:0] salida,
  output carry_out
);

  wire alu_op0, alu_op1, alu_op2, and_1_out, clock, imm_we, in_en, j_cond, j_inc, nor_1_out, not_1_out,
       not_2_out, or_1_out, out_we, reg_en, reg_we, regA_we, zero;
  wire [7:0] alu_1_salida, bancoreg_1_salida, controlled_buffer_1_out, ir_1__0_7, ir_1__8_15, j_address,
       registro_2_salida;
  wire [15:0] rom_1_instruccion;

  Clock Reloj (.out(clock));
  DU du_1 (
    .IR13(ir_1__8_15[5]), .IR12(ir_1__8_15[4]), .IR11(ir_1__8_15[3]), .IR10(ir_1__8_15[2]),
    .IR09(ir_1__8_15[1]), .IR08(ir_1__8_15[0]), .reg_en(reg_en), .alu_op2(alu_op2), .alu_op1(alu_op1),
    .regA_we(regA_we), .out_we(out_we), .reg_we(reg_we), .in_en(in_en), .alu_op0(alu_op0), .inm_we(imm_we),
    .j_inc(j_inc), .J_cond(j_cond));
  // Probe on ir_1__8_15
  Registro registro_1 (.entrada(alu_1_salida), .clock(clock), .reset(in_1), .we(out_we), .salida(salida));
  // Probe on rom_1_instruccion
  IR ir_1 (.entrada(rom_1_instruccion), .reset(in_1), .clock(clock), .we(1'b1), ._0_7(ir_1__0_7), ._8_15(ir_1__8_15));
  // Probe on ir_1__0_7[3:0]
  // Probe on ir_1__0_7[7:4]
  BancoReg bancoreg_1 (
    .rs(ir_1__0_7[3:0]), .rd(ir_1__0_7[7:4]), .salida(bancoreg_1_salida), .reset(in_1), .clock(clock),
    .entrada(alu_1_salida), .we(reg_we));
  // Probe on alu_1_salida
  // Probe on j_address
  ROM rom_1 (
    .clock(not_1_out), .j_enable(or_1_out), .Reset(in_1), .instruccion(rom_1_instruccion),
    .j_address(j_address));
  // Probe on ir_1__0_7
  assign controlled_buffer_1_out = reg_en ? bancoreg_1_salida : 8'bz;  // Controlled_Buffer controlled_buffer_1
  not not_1 (not_1_out, clock);
  assign controlled_buffer_1_out = imm_we ? ir_1__0_7 : 8'bz;  // Controlled_Buffer controlled_buffer_2
  or or_1 (or_1_out, j_inc, and_1_out);
  // Probe on controlled_buffer_1_out
  Registro registro_2 (
    .entrada(controlled_buffer_1_out), .clock(clock), .reset(in_1), .we(regA_we), .salida(registro_2_salida));
  // Probe on registro_2_salida
  and and_1 (and_1_out, j_cond, zero);
  assign controlled_buffer_1_out = in_en ? in_2 : 8'bz;  // Controlled_Buffer controlled_buffer_3
  Register register_1 (.D(controlled_buffer_1_out), .en(1'b1), .Q(j_address), .clk(not_2_out), .clr(in_1));
  not not_2 (not_2_out, clock);
  // Probe on alu_1_salida
  ALU alu_1 (
    .a(controlled_buffer_1_out), .b(registro_2_salida), .carry_out(carry_out), .op2(alu_op2), .op1(alu_op1),
    .op0(alu_op0), .salida(alu_1_salida));
  // Probe on j_address
  nor nor_1 (nor_1_out, alu_1_salida[0], alu_1_salida[1], alu_1_salida[2], alu_1_salida[3], alu_1_salida[4], alu_1_salida[5], alu_1_salida[6], alu_1_salida[7]);
  D_Flip_Flop d_ff_1 (.clk(clock), .D(nor_1_out), .Q(zero), .reset(in_1));  // open: Qn, preset, en

  // Other names for the same wires on the sheet: reset = in_1

  // Notes on the sheet:
  //   rs
  //   rd
  //   0
  //   0
  //   0
  //   0
  //   1
  //   0
  //   0
  //   1
  //   0
  //   1
  //   1
  //   0
  //   1
  //   1
  //   1
  //   1
  //   op2
  //   op1
  //   a
  //   0
  //   a << 1
  //   1
  //   a + b
  //   0
  //   a - b
  //   1
  //   a and b
  //   0
  //   1
  //   a or b
  //   a xor b
  //   0
  //   1
  //   a >> 1
  //   op0
endmodule

module DU (
  input  IR13,
  input  IR12,
  input  IR11,
  input  IR10,
  input  IR09,
  input  IR08,
  output reg_en,
  output alu_op2,
  output alu_op1,
  output regA_we,
  output out_we,
  output reg_we,
  output in_en,
  output alu_op0,
  output inm_we,
  output j_inc,
  output J_cond
);

  wire and_1_out, and_2_out, and_3_out, and_4_out, and_5_out, and_6_out, and_7_out, and_8_out, and_9_out,
       and_10_out, and_13_out, and_14_out, and_15_out, and_16_out, and_18_out, and_19_out, and_20_out,
       and_21_out, and_23_out, and_24_out, not_1_out, not_2_out, not_3_out, not_4_out, not_5_out, not_6_out,
       not_7_out, not_8_out, not_9_out, not_10_out, not_11_out, not_12_out, not_13_out, not_14_out,
       not_15_out, not_16_out, not_17_out, not_18_out, not_19_out, not_20_out, not_21_out, not_22_out,
       not_23_out, not_24_out, not_25_out, not_26_out, not_27_out, not_28_out, not_29_out, not_30_out,
       not_31_out, not_32_out, not_33_out, not_34_out, not_35_out, not_36_out, not_37_out, not_38_out,
       not_39_out, not_40_out, not_41_out, not_42_out, not_43_out, not_44_out, not_45_out, not_46_out,
       not_47_out, not_48_out, not_49_out, not_50_out, not_51_out, not_52_out, not_53_out, not_54_out,
       not_55_out, not_56_out, not_57_out, not_58_out, not_59_out, not_60_out, not_61_out, not_62_out,
       not_63_out, not_64_out, not_65_out, not_66_out, not_67_out, not_68_out, not_69_out, not_70_out,
       not_71_out, not_72_out, not_73_out, not_74_out, not_75_out, not_76_out, not_77_out, not_78_out,
       not_79_out, not_80_out, not_81_out, not_82_out, not_83_out, not_84_out, not_85_out, not_86_out,
       not_87_out, not_88_out, not_89_out;

  not not_1 (not_1_out, IR13);
  not not_2 (not_2_out, IR11);
  not not_3 (not_3_out, IR10);
  not not_4 (not_4_out, IR13);
  not not_5 (not_5_out, IR11);
  not not_6 (not_6_out, IR09);
  not not_7 (not_7_out, IR08);
  not not_8 (not_8_out, IR13);
  not not_9 (not_9_out, IR11);
  not not_10 (not_10_out, IR10);
  not not_11 (not_11_out, IR12);
  not not_12 (not_12_out, IR11);
  not not_13 (not_13_out, IR10);
  not not_14 (not_14_out, IR09);
  not not_15 (not_15_out, IR13);
  not not_16 (not_16_out, IR11);
  not not_17 (not_17_out, IR10);
  not not_18 (not_18_out, IR13);
  not not_19 (not_19_out, IR11);
  not not_20 (not_20_out, IR09);
  not not_21 (not_21_out, IR08);
  not not_22 (not_22_out, IR12);
  not not_23 (not_23_out, IR11);
  not not_24 (not_24_out, IR10);
  not not_25 (not_25_out, IR09);
  not not_26 (not_26_out, IR13);
  not not_27 (not_27_out, IR11);
  not not_28 (not_28_out, IR10);
  not not_29 (not_29_out, IR09);
  not not_30 (not_30_out, IR13);
  not not_31 (not_31_out, IR11);
  not not_32 (not_32_out, IR09);
  not not_33 (not_33_out, IR08);
  not not_34 (not_34_out, IR12);
  not not_35 (not_35_out, IR11);
  not not_36 (not_36_out, IR10);
  not not_37 (not_37_out, IR09);
  not not_38 (not_38_out, IR13);
  not not_39 (not_39_out, IR12);
  not not_40 (not_40_out, IR11);
  not not_41 (not_41_out, IR09);
  not not_42 (not_42_out, IR13);
  not not_43 (not_43_out, IR12);
  not not_44 (not_44_out, IR11);
  not not_45 (not_45_out, IR10);
  not not_46 (not_46_out, IR08);
  not not_47 (not_47_out, IR13);
  not not_48 (not_48_out, IR11);
  not not_49 (not_49_out, IR10);
  not not_50 (not_50_out, IR13);
  not not_51 (not_51_out, IR11);
  not not_52 (not_52_out, IR10);
  not not_53 (not_53_out, IR13);
  not not_54 (not_54_out, IR11);
  not not_55 (not_55_out, IR09);
  not not_56 (not_56_out, IR08);
  not not_57 (not_57_out, IR12);
  not not_58 (not_58_out, IR11);
  not not_59 (not_59_out, IR10);
  not not_60 (not_60_out, IR09);
  not not_61 (not_61_out, IR13);
  not not_62 (not_62_out, IR12);
  not not_63 (not_63_out, IR11);
  not not_64 (not_64_out, IR10);
  not not_65 (not_65_out, IR09);
  not not_66 (not_66_out, IR13);
  not not_67 (not_67_out, IR11);
  not not_68 (not_68_out, IR10);
  not not_69 (not_69_out, IR12);
  not not_70 (not_70_out, IR11);
  not not_71 (not_71_out, IR10);
  not not_72 (not_72_out, IR09);
  not not_73 (not_73_out, IR13);
  not not_74 (not_74_out, IR12);
  not not_75 (not_75_out, IR11);
  not not_76 (not_76_out, IR09);
  not not_77 (not_77_out, IR11);
  not not_78 (not_78_out, IR10);
  not not_79 (not_79_out, IR09);
  not not_80 (not_80_out, IR11);
  not not_81 (not_81_out, IR10);
  not not_82 (not_82_out, IR09);
  not not_83 (not_83_out, IR08);
  not not_84 (not_84_out, IR11);
  not not_85 (not_85_out, IR10);
  not not_86 (not_86_out, IR09);
  not not_87 (not_87_out, IR11);
  not not_88 (not_88_out, IR10);
  not not_89 (not_89_out, IR08);
  and and_1 (and_1_out, not_1_out, not_2_out, not_3_out, IR09);
  and and_2 (and_2_out, not_4_out, not_5_out, IR10, not_6_out, not_7_out);
  and and_3 (and_3_out, not_8_out, IR12, not_9_out, not_10_out);
  and and_4 (and_4_out, IR13, not_11_out, not_12_out, not_13_out, not_14_out);
  and and_5 (and_5_out, not_15_out, IR12, not_16_out, not_17_out, IR09);
  and and_6 (and_6_out, not_18_out, IR12, not_19_out, IR10, not_20_out, not_21_out);
  and and_7 (and_7_out, IR13, not_22_out, not_23_out, not_24_out, not_25_out, IR08);
  and and_8 (and_8_out, not_26_out, IR12, not_27_out, not_28_out, not_29_out);
  and and_9 (and_9_out, not_30_out, IR12, not_31_out, not_32_out, not_33_out);
  and and_10 (and_10_out, IR13, not_34_out, not_35_out, not_36_out, not_37_out, IR08);
  and and_11 (regA_we, not_38_out, not_39_out, not_40_out, IR10, not_41_out);
  and and_12 (out_we, not_42_out, not_43_out, not_44_out, not_45_out, IR09, not_46_out);
  and and_13 (and_13_out, not_47_out, not_48_out, not_49_out, IR08);
  and and_14 (and_14_out, not_50_out, IR12, not_51_out, not_52_out);
  and and_15 (and_15_out, not_53_out, IR12, not_54_out, not_55_out, not_56_out);
  and and_16 (and_16_out, IR13, not_57_out, not_58_out, not_59_out, not_60_out);
  and and_17 (in_en, not_61_out, not_62_out, not_63_out, not_64_out, not_65_out, IR08);
  and and_18 (and_18_out, not_66_out, IR12, not_67_out, not_68_out, IR08);
  and and_19 (and_19_out, IR13, not_69_out, not_70_out, not_71_out, not_72_out);
  and and_20 (and_20_out, not_73_out, not_74_out, not_75_out, IR10, not_76_out, IR08);
  and and_21 (and_21_out, IR13, IR12, not_77_out, not_78_out, not_79_out);
  and and_22 (j_inc, IR13, IR12, not_80_out, not_81_out, not_82_out, not_83_out);
  and and_23 (and_23_out, IR13, IR12, not_84_out, not_85_out, not_86_out, IR08);
  and and_24 (and_24_out, IR13, IR12, not_87_out, not_88_out, IR09, not_89_out);
  or or_1 (reg_en, and_1_out, and_2_out, and_3_out, and_4_out);
  or or_2 (alu_op2, and_5_out, and_6_out, and_7_out);
  or or_3 (alu_op1, and_8_out, and_9_out, and_10_out);
  or or_4 (reg_we, and_13_out, and_14_out, and_15_out, and_16_out);
  or or_5 (alu_op0, and_18_out, and_19_out);
  or or_6 (inm_we, and_20_out, and_21_out);
  or or_7 (J_cond, and_23_out, and_24_out);
endmodule

// Reg_out
module Registro (
  input  clock,
  input  reset,
  input  [7:0] entrada,
  input  we,
  output [7:0] salida
);

  D_Flip_Flop d_ff_1 (.clk(clock), .D(entrada[0]), .Q(salida[0]), .en(we), .reset(reset));  // open: Qn, preset
  D_Flip_Flop d_ff_2 (.clk(clock), .D(entrada[1]), .Q(salida[1]), .en(we), .reset(reset));  // open: Qn, preset
  D_Flip_Flop d_ff_3 (.clk(clock), .D(entrada[2]), .Q(salida[2]), .en(we), .reset(reset));  // open: Qn, preset
  D_Flip_Flop d_ff_4 (.clk(clock), .D(entrada[3]), .Q(salida[3]), .en(we), .reset(reset));  // open: Qn, preset
  D_Flip_Flop d_ff_5 (.clk(clock), .D(entrada[4]), .Q(salida[4]), .en(we), .reset(reset));  // open: Qn, preset
  D_Flip_Flop d_ff_6 (.clk(clock), .D(entrada[5]), .Q(salida[5]), .en(we), .reset(reset));  // open: Qn, preset
  D_Flip_Flop d_ff_7 (.clk(clock), .D(entrada[6]), .Q(salida[6]), .en(we), .reset(reset));  // open: Qn, preset
  D_Flip_Flop d_ff_8 (.clk(clock), .D(entrada[7]), .Q(salida[7]), .en(we), .reset(reset));  // open: Qn, preset
endmodule

module IR (
  input  reset,
  input  [15:0] entrada,
  input  clock,
  input  we,
  output [7:0] _0_7,
  output [7:0] _8_15
);

  Registro registro_1 (.entrada(entrada[7:0]), .clock(clock), .reset(reset), .we(we), .salida(_0_7));
  Registro registro_2 (.entrada(entrada[15:8]), .clock(clock), .reset(reset), .we(we), .salida(_8_15));
endmodule

module ALU (
  input  [7:0] a,
  input  [7:0] b,
  input  op2,
  input  op1,
  input  op0,
  output carry_out,
  output [7:0] salida
);

  wire [7:0] and_x8_1_out_3, desplazar_derecha_1_out_2, desplazar_izq_1_out_2, full_adder_8bits_1_r,
       or_x8_1_out_3, xor_x8_1_out_3, xor_x8_2_out_3;

  desplazar_izq desplazar_izq_1 (.in_1(a), .out_2(desplazar_izq_1_out_2));
  XOR_x8 xor_x8_1 (.in_1(b), .in_2({8{op0}}), .out_3(xor_x8_1_out_3));
  AND_x8 and_x8_1 (.in_1(a), .in_2(b), .out_3(and_x8_1_out_3));
  full_adder_8bits full_adder_8bits_1 (
    .in_1(op0), .B(a), .A(xor_x8_1_out_3), .R(full_adder_8bits_1_r), .out_5(carry_out));
  OR_x8 or_x8_1 (.in_1(a), .in_2(b), .out_3(or_x8_1_out_3));
  XOR_x8 xor_x8_2 (.in_1(a), .in_2(b), .out_3(xor_x8_2_out_3));
  desplazar_derecha desplazar_derecha_1 (.in_1(a), .out_2(desplazar_derecha_1_out_2));
  mux_4x8_8 mux_4x8_8_1 (
    .in_1(a), .in_2(desplazar_izq_1_out_2), .in_3(full_adder_8bits_1_r), .in_4(full_adder_8bits_1_r),
    .in_5(and_x8_1_out_3), .in_6(or_x8_1_out_3), .in_7(xor_x8_2_out_3), .in_8(desplazar_derecha_1_out_2),
    .in_9(op2), .in_10(op1), .in_11(op0), .out_12(salida));

  // Other names for the same wires on the sheet: t1 = op0; t2[7:0] = {8{op0}}

  // Notes on the sheet:
  //   0
  //   0
  //   0
  //   0
  //   0
  //   1
  //   0
  //   1
  //   0
  //   1
  //   0
  //   1
  //   1
  //   1
  //   1
  //   1
  //   0
  //   1
  //   0
  //   1
  //   0
  //   1
  //   0
  //   1
  //   a
  //   a << 1
  //   a + b
  //   a - b
  //   a and b
  //   a or b
  //   a xor b
  //   a >> 1
endmodule

module BancoReg (
  input  [3:0] rs,
  input  reset,
  input  clock,
  input  [7:0] entrada,
  input  [3:0] rd,
  input  we,
  output [7:0] salida
);

  wire demultiplexer_1_out0, demultiplexer_1_out1, demultiplexer_1_out2, demultiplexer_1_out3,
       demultiplexer_1_out4, demultiplexer_1_out5, demultiplexer_1_out6, demultiplexer_1_out7,
       demultiplexer_1_out8, demultiplexer_1_out9, demultiplexer_1_out10, demultiplexer_1_out11,
       demultiplexer_1_out12, demultiplexer_1_out13, demultiplexer_1_out14, demultiplexer_1_out15,
       demultiplexer_2_out0, demultiplexer_2_out1, demultiplexer_2_out2, demultiplexer_2_out3,
       demultiplexer_2_out4, demultiplexer_2_out5, demultiplexer_2_out6, demultiplexer_2_out7,
       demultiplexer_2_out8, demultiplexer_2_out9, demultiplexer_2_out10, demultiplexer_2_out11,
       demultiplexer_2_out12, demultiplexer_2_out13, demultiplexer_2_out14, demultiplexer_2_out15;
  wire [7:0] registro_1_salida, registro_2_salida, registro_3_salida, registro_4_salida, registro_5_salida,
       registro_6_salida, registro_7_salida, registro_8_salida, registro_9_salida, registro_10_salida,
       registro_11_salida, registro_12_salida, registro_13_salida, registro_14_salida, registro_15_salida,
       registro_16_salida;

  assign salida = demultiplexer_1_out0 ? registro_1_salida : 8'bz;  // Controlled_Buffer controlled_buffer_1
  Registro registro_1 (
    .entrada(entrada), .clock(clock), .reset(reset), .we(demultiplexer_2_out0), .salida(registro_1_salida));
  assign salida = demultiplexer_1_out1 ? registro_2_salida : 8'bz;  // Controlled_Buffer controlled_buffer_2
  Registro registro_2 (
    .entrada(entrada), .clock(clock), .reset(reset), .we(demultiplexer_2_out1), .salida(registro_2_salida));
  assign salida = demultiplexer_1_out2 ? registro_3_salida : 8'bz;  // Controlled_Buffer controlled_buffer_3
  Registro registro_3 (
    .entrada(entrada), .clock(clock), .reset(reset), .we(demultiplexer_2_out2), .salida(registro_3_salida));
  assign salida = demultiplexer_1_out3 ? registro_4_salida : 8'bz;  // Controlled_Buffer controlled_buffer_4
  Registro registro_4 (
    .entrada(entrada), .clock(clock), .reset(reset), .we(demultiplexer_2_out3), .salida(registro_4_salida));
  assign salida = demultiplexer_1_out4 ? registro_6_salida : 8'bz;  // Controlled_Buffer controlled_buffer_5
  assign salida = demultiplexer_1_out5 ? registro_5_salida : 8'bz;  // Controlled_Buffer controlled_buffer_6
  Registro registro_5 (
    .entrada(entrada), .clock(clock), .reset(reset), .we(demultiplexer_2_out5), .salida(registro_5_salida));
  Registro registro_6 (
    .entrada(entrada), .clock(clock), .reset(reset), .we(demultiplexer_2_out4), .salida(registro_6_salida));
  assign salida = demultiplexer_1_out6 ? registro_7_salida : 8'bz;  // Controlled_Buffer controlled_buffer_7
  Registro registro_7 (
    .entrada(entrada), .clock(clock), .reset(reset), .we(demultiplexer_2_out6), .salida(registro_7_salida));
  Demultiplexer #(.select(4)) demultiplexer_1 (
    .out0(demultiplexer_1_out0), .out1(demultiplexer_1_out1), .out2(demultiplexer_1_out2),
    .out3(demultiplexer_1_out3), .out4(demultiplexer_1_out4), .out5(demultiplexer_1_out5),
    .out6(demultiplexer_1_out6), .out7(demultiplexer_1_out7), .out8(demultiplexer_1_out8),
    .out9(demultiplexer_1_out9), .out10(demultiplexer_1_out10), .out11(demultiplexer_1_out11),
    .out12(demultiplexer_1_out12), .out13(demultiplexer_1_out13), .out14(demultiplexer_1_out14),
    .out15(demultiplexer_1_out15), .in(1'b1), .sel(rs));  // open: en
  assign salida = demultiplexer_1_out7 ? registro_8_salida : 8'bz;  // Controlled_Buffer controlled_buffer_8
  Registro registro_8 (
    .entrada(entrada), .clock(clock), .reset(reset), .we(demultiplexer_2_out7), .salida(registro_8_salida));
  Demultiplexer #(.select(4)) demultiplexer_2 (
    .out0(demultiplexer_2_out0), .out1(demultiplexer_2_out1), .out2(demultiplexer_2_out2),
    .out3(demultiplexer_2_out3), .out4(demultiplexer_2_out4), .out5(demultiplexer_2_out5),
    .out6(demultiplexer_2_out6), .out7(demultiplexer_2_out7), .out8(demultiplexer_2_out8),
    .out9(demultiplexer_2_out9), .out10(demultiplexer_2_out10), .out11(demultiplexer_2_out11),
    .out12(demultiplexer_2_out12), .out13(demultiplexer_2_out13), .out14(demultiplexer_2_out14),
    .out15(demultiplexer_2_out15), .in(we), .sel(rd));  // open: en
  assign salida = demultiplexer_1_out8 ? registro_9_salida : 8'bz;  // Controlled_Buffer controlled_buffer_9
  Registro registro_9 (
    .entrada(entrada), .clock(clock), .reset(reset), .we(demultiplexer_2_out8), .salida(registro_9_salida));
  assign salida = demultiplexer_1_out9 ? registro_10_salida : 8'bz;  // Controlled_Buffer controlled_buffer_10
  Registro registro_10 (
    .entrada(entrada), .clock(clock), .reset(reset), .we(demultiplexer_2_out9), .salida(registro_10_salida));
  assign salida = demultiplexer_1_out10 ? registro_11_salida : 8'bz;  // Controlled_Buffer controlled_buffer_11
  Registro registro_11 (
    .entrada(entrada), .clock(clock), .reset(reset), .we(demultiplexer_2_out10), .salida(registro_11_salida));
  assign salida = demultiplexer_1_out11 ? registro_12_salida : 8'bz;  // Controlled_Buffer controlled_buffer_12
  Registro registro_12 (
    .entrada(entrada), .clock(clock), .reset(reset), .we(demultiplexer_2_out11), .salida(registro_12_salida));
  assign salida = demultiplexer_1_out12 ? registro_13_salida : 8'bz;  // Controlled_Buffer controlled_buffer_13
  assign salida = demultiplexer_1_out13 ? registro_14_salida : 8'bz;  // Controlled_Buffer controlled_buffer_14
  Registro registro_13 (
    .entrada(entrada), .clock(clock), .reset(reset), .we(demultiplexer_2_out12), .salida(registro_13_salida));
  Registro registro_14 (
    .entrada(entrada), .clock(clock), .reset(reset), .we(demultiplexer_2_out13), .salida(registro_14_salida));
  assign salida = demultiplexer_1_out14 ? registro_15_salida : 8'bz;  // Controlled_Buffer controlled_buffer_15
  Registro registro_15 (
    .entrada(entrada), .clock(clock), .reset(reset), .we(demultiplexer_2_out14), .salida(registro_15_salida));
  assign salida = demultiplexer_1_out15 ? registro_16_salida : 8'bz;  // Controlled_Buffer controlled_buffer_16
  Registro registro_16 (
    .entrada(entrada), .clock(clock), .reset(reset), .we(demultiplexer_2_out15), .salida(registro_16_salida));
endmodule

module ROM (
  input  clock,
  input  j_enable,
  input  Reset,
  input  [7:0] j_address,
  output [15:0] instruccion
);

  wire or_1_out;
  wire [7:0] contador_1_address, multiplexer_1_out;

  contador contador_1 (
    .clock(clock), .jump_enable(or_1_out), .j_address(multiplexer_1_out), .address(contador_1_address));
  or or_1 (or_1_out, j_enable, Reset);
  Multiplexer #(.width(8)) multiplexer_1 (
    .in0(j_address), .in1({8{1'b0}}), .out(multiplexer_1_out), .sel(Reset));  // open: en
  ROM_part #(.dataWidth(16)) rom_1 (.addr(contador_1_address), .data(instruccion));  // open: sel

  // Notes on the sheet:
  //   contents of rom_1 (hex, n*v repeats v):
  //   130 500 1211 1222 508 1311 1322 501 1243 310e 2133 1122 3110 3008 1111 300a 201
endmodule

module contador (
  input  clock,
  input  jump_enable,
  input  [7:0] j_address,
  output [7:0] address
);

  wire and_1_out, and_2_out, and_3_out, and_4_out, and_5_out, and_6_out, set_address_contador_1_al_lsb,
       set_address_contador_1_out_4, set_address_contador_1_out_5, set_address_contador_1_out_6,
       set_address_contador_1_out_7, set_address_contador_1_out_8, set_address_contador_1_out_9,
       set_address_contador_1_out_10, set_address_contador_1_out_11, set_address_contador_1_out_12,
       set_address_contador_1_out_13, set_address_contador_1_out_14, set_address_contador_1_out_15,
       set_address_contador_1_out_16, set_address_contador_1_out_17, set_address_contador_1_out_18;

  set_address_contador set_address_contador_1 (
    .enciende_apaga(jump_enable), .address(j_address), .al_LSB(set_address_contador_1_al_lsb),
    .out_4(set_address_contador_1_out_4), .out_5(set_address_contador_1_out_5),
    .out_6(set_address_contador_1_out_6), .out_7(set_address_contador_1_out_7),
    .out_8(set_address_contador_1_out_8), .out_9(set_address_contador_1_out_9),
    .out_10(set_address_contador_1_out_10), .out_11(set_address_contador_1_out_11),
    .out_12(set_address_contador_1_out_12), .out_13(set_address_contador_1_out_13),
    .out_14(set_address_contador_1_out_14), .out_15(set_address_contador_1_out_15),
    .out_16(set_address_contador_1_out_16), .out_17(set_address_contador_1_out_17),
    .out_18(set_address_contador_1_out_18));
  T_Flip_Flop t_ff_1 (
    .clk(clock), .T(1'b1), .Q(address[0]), .preset(set_address_contador_1_al_lsb),
    .reset(set_address_contador_1_out_4));  // open: Qn, en
  T_Flip_Flop t_ff_2 (
    .clk(clock), .T(address[0]), .Q(address[1]), .preset(set_address_contador_1_out_5),
    .reset(set_address_contador_1_out_6));  // open: Qn, en
  and and_1 (and_1_out, address[1], address[0]);
  T_Flip_Flop t_ff_3 (
    .clk(clock), .T(and_1_out), .Q(address[2]), .preset(set_address_contador_1_out_7),
    .reset(set_address_contador_1_out_8));  // open: Qn, en
  and and_2 (and_2_out, address[2], and_1_out);
  T_Flip_Flop t_ff_4 (
    .clk(clock), .T(and_2_out), .Q(address[3]), .preset(set_address_contador_1_out_9),
    .reset(set_address_contador_1_out_10));  // open: Qn, en
  and and_3 (and_3_out, address[3], and_2_out);
  T_Flip_Flop t_ff_5 (
    .clk(clock), .T(and_3_out), .Q(address[4]), .preset(set_address_contador_1_out_11),
    .reset(set_address_contador_1_out_12));  // open: Qn, en
  and and_4 (and_4_out, address[4], and_3_out);
  T_Flip_Flop t_ff_6 (
    .clk(clock), .T(and_4_out), .Q(address[5]), .preset(set_address_contador_1_out_13),
    .reset(set_address_contador_1_out_14));  // open: Qn, en
  and and_5 (and_5_out, address[5], and_4_out);
  T_Flip_Flop t_ff_7 (
    .clk(clock), .T(and_5_out), .Q(address[6]), .preset(set_address_contador_1_out_15),
    .reset(set_address_contador_1_out_16));  // open: Qn, en
  and and_6 (and_6_out, address[6], and_5_out);
  T_Flip_Flop t_ff_8 (
    .clk(clock), .T(and_6_out), .Q(address[7]), .preset(set_address_contador_1_out_17),
    .reset(set_address_contador_1_out_18));  // open: Qn, en
endmodule

module FF_D_con_Latch_D (
  input  preset,
  input  D,
  input  reset,
  input  clock,
  output Q,
  output minus_Q
);

  wire latch_d_1_q, not_1_out;

  latch_D latch_d_1 (.D(D), .H(not_1_out), .preset(preset), .reset(reset), .Q(latch_d_1_q));  // open: minus_Q
  not not_1 (not_1_out, clock);
  latch_D latch_d_2 (.D(latch_d_1_q), .H(clock), .preset(preset), .reset(reset), .Q(Q), .minus_Q(minus_Q));
endmodule

module mux_2x8_8 (
  input  [7:0] in_1,
  input  [7:0] in_2,
  input  in_3,
  output [7:0] out_4
);

  ALU_mux_2x1_1 mux_2x1_1_1 (.A(in_1[0]), .B(in_2[0]), .in_3(in_3), .out_4(out_4[0]));
  ALU_mux_2x1_1 mux_2x1_1_2 (.A(in_1[1]), .B(in_2[1]), .in_3(in_3), .out_4(out_4[1]));
  ALU_mux_2x1_1 mux_2x1_1_3 (.A(in_1[2]), .B(in_2[2]), .in_3(in_3), .out_4(out_4[2]));
  ALU_mux_2x1_1 mux_2x1_1_4 (.A(in_1[3]), .B(in_2[3]), .in_3(in_3), .out_4(out_4[3]));
  ALU_mux_2x1_1 mux_2x1_1_5 (.A(in_1[4]), .B(in_2[4]), .in_3(in_3), .out_4(out_4[4]));
  ALU_mux_2x1_1 mux_2x1_1_6 (.A(in_1[5]), .B(in_2[5]), .in_3(in_3), .out_4(out_4[5]));
  ALU_mux_2x1_1 mux_2x1_1_7 (.A(in_1[6]), .B(in_2[6]), .in_3(in_3), .out_4(out_4[6]));
  ALU_mux_2x1_1 mux_2x1_1_8 (.A(in_1[7]), .B(in_2[7]), .in_3(in_3), .out_4(out_4[7]));
endmodule

module mux_4x8_8 (
  input  [7:0] in_1,
  input  [7:0] in_2,
  input  [7:0] in_3,
  input  [7:0] in_4,
  input  [7:0] in_5,
  input  [7:0] in_6,
  input  [7:0] in_7,
  input  [7:0] in_8,
  input  in_9,
  input  in_10,
  input  in_11,
  output [7:0] out_12
);

  wire [7:0] mux_2x8_8_1_out_4, mux_2x8_8_2_out_4, mux_2x8_8_3_out_4, mux_2x8_8_4_out_4, mux_2x8_8_5_out_4,
       mux_2x8_8_6_out_4;

  mux_2x8_8 mux_2x8_8_1 (.in_1(in_1), .in_2(in_2), .in_3(in_11), .out_4(mux_2x8_8_1_out_4));
  mux_2x8_8 mux_2x8_8_2 (.in_1(in_3), .in_2(in_4), .in_3(in_11), .out_4(mux_2x8_8_2_out_4));
  mux_2x8_8 mux_2x8_8_3 (.in_1(in_5), .in_2(in_6), .in_3(in_11), .out_4(mux_2x8_8_3_out_4));
  mux_2x8_8 mux_2x8_8_4 (.in_1(in_7), .in_2(in_8), .in_3(in_11), .out_4(mux_2x8_8_4_out_4));
  mux_2x8_8 mux_2x8_8_5 (.in_1(mux_2x8_8_1_out_4), .in_2(mux_2x8_8_2_out_4), .in_3(in_10), .out_4(mux_2x8_8_5_out_4));
  mux_2x8_8 mux_2x8_8_6 (.in_1(mux_2x8_8_3_out_4), .in_2(mux_2x8_8_4_out_4), .in_3(in_10), .out_4(mux_2x8_8_6_out_4));
  mux_2x8_8 mux_2x8_8_7 (.in_1(mux_2x8_8_5_out_4), .in_2(mux_2x8_8_6_out_4), .in_3(in_9), .out_4(out_12));
endmodule

module mux_2x1_1 (
  input  A,
  input  B,
  input  in_3,
  output out_4
);

  wire and_1_out, and_2_out, not_1_out;

  not not_1 (not_1_out, in_3);
  and and_1 (and_1_out, A, not_1_out);
  and and_2 (and_2_out, B, in_3);
  or or_1 (out_4, and_1_out, and_2_out);
endmodule

module latch_S_R (
  input  Preset,
  input  e1,
  input  Habilitacion,
  input  e2,
  input  Reset,
  output Q,
  output minus_Q
);

  wire nand_1_out, nand_2_out, nand_3_out, nand_4_out;

  nand nand_1 (nand_1_out, e1, Habilitacion);
  nand nand_2 (nand_2_out, Habilitacion, e2);
  nand nand_3 (nand_3_out, nand_1_out, minus_Q);
  nand nand_4 (nand_4_out, Q, nand_2_out);
  or or_1 (Q, Preset, nand_3_out);
  or or_2 (minus_Q, nand_4_out, Reset);
endmodule

module latch_D (
  input  preset,
  input  D,
  input  H,
  input  reset,
  output Q,
  output minus_Q
);

  wire not_1_out;

  not not_1 (not_1_out, D);
  latch_S_R latch_s_r_1 (
    .e1(D), .Habilitacion(H), .e2(not_1_out), .Preset(preset), .Reset(reset), .Q(Q), .minus_Q(minus_Q));
endmodule
